// Logisim project Project.circ as structural Verilog: 4 circuits, main circuit Register_File
module Register_File (
  input  Clk,
  input  [7:0] Write_Data,
  input  Write,
  input  [4:0] Write_address,
  input  [4:0] Read_address_1,
  input  [4:0] Read_address_2,
  output [7:0] Read_Data_1,
  output [7:0] Read_Data_2
);

  wire decoder_1_out0, decoder_1_out1, decoder_1_out2, decoder_1_out3, decoder_1_out4, decoder_1_out5,
       decoder_1_out6, decoder_1_out7, decoder_1_out8, decoder_1_out9, decoder_1_out10, decoder_1_out11,
       decoder_1_out12, decoder_1_out13, decoder_1_out14, decoder_1_out15, decoder_1_out16, decoder_1_out17,
       decoder_1_out18, decoder_1_out19, decoder_1_out20, decoder_1_out21, decoder_1_out22, decoder_1_out23,
       decoder_1_out24, decoder_1_out25, decoder_1_out26, decoder_1_out27, decoder_1_out28, decoder_1_out29,
       decoder_1_out30, decoder_1_out31;
  wire [7:0] R0_q, R1_q, R2_q, R3_q, R4_q, R5_q, R6_q, R7_q, R8_q, R9_q, R10_q, R11_q, R12_q, R13_q, R14_q,
       R15_q, R16_q, R17_q, R18_q, R19_q, R20_q, R21_q, R22_q, R23_q, R24_q, R25_q, R26_q, R27_q, R28_q,
       R29_q, R30_q, R31_q;

  Decoder #(.select(5)) decoder_1 (
    .out0(decoder_1_out0), .out1(decoder_1_out1), .out2(decoder_1_out2), .out3(decoder_1_out3),
    .out4(decoder_1_out4), .out5(decoder_1_out5), .out6(decoder_1_out6), .out7(decoder_1_out7),
    .out8(decoder_1_out8), .out9(decoder_1_out9), .out10(decoder_1_out10), .out11(decoder_1_out11),
    .out12(decoder_1_out12), .out13(decoder_1_out13), .out14(decoder_1_out14), .out15(decoder_1_out15),
    .out16(decoder_1_out16), .out17(decoder_1_out17), .out18(decoder_1_out18), .out19(decoder_1_out19),
    .out20(decoder_1_out20), .out21(decoder_1_out21), .out22(decoder_1_out22), .out23(decoder_1_out23),
    .out24(decoder_1_out24), .out25(decoder_1_out25), .out26(decoder_1_out26), .out27(decoder_1_out27),
    .out28(decoder_1_out28), .out29(decoder_1_out29), .out30(decoder_1_out30), .out31(decoder_1_out31),
    .sel(Write_address), .en(Write));
  Register R0 (.D(Write_Data), .en(decoder_1_out0), .clk(Clk), .Q(R0_q));  // open: clr
  Register R8 (.D(Write_Data), .en(decoder_1_out8), .clk(Clk), .Q(R8_q));  // open: clr
  Register R16 (.D(Write_Data), .en(decoder_1_out16), .clk(Clk), .Q(R16_q));  // open: clr
  Register R24 (.D(Write_Data), .en(decoder_1_out24), .clk(Clk), .Q(R24_q));  // open: clr
  Register R1 (.D(Write_Data), .en(decoder_1_out1), .clk(Clk), .Q(R1_q));  // open: clr
  Register R9 (.D(Write_Data), .en(decoder_1_out9), .clk(Clk), .Q(R9_q));  // open: clr
  Register R17 (.D(Write_Data), .en(decoder_1_out17), .clk(Clk), .Q(R17_q));  // open: clr
  Register R25 (.D(Write_Data), .en(decoder_1_out25), .clk(Clk), .Q(R25_q));  // open: clr
  Register R2 (.D(Write_Data), .en(decoder_1_out2), .clk(Clk), .Q(R2_q));  // open: clr
  Register R10 (.D(Write_Data), .en(decoder_1_out10), .clk(Clk), .Q(R10_q));  // open: clr
  Register R18 (.D(Write_Data), .en(decoder_1_out18), .clk(Clk), .Q(R18_q));  // open: clr
  Register R26 (.D(Write_Data), .en(decoder_1_out26), .clk(Clk), .Q(R26_q));  // open: clr
  Register R3 (.D(Write_Data), .en(decoder_1_out3), .clk(Clk), .Q(R3_q));  // open: clr
  Register R11 (.D(Write_Data), .en(decoder_1_out11), .clk(Clk), .Q(R11_q));  // open: clr
  Register R19 (.D(Write_Data), .en(decoder_1_out19), .clk(Clk), .Q(R19_q));  // open: clr
  Register R27 (.D(Write_Data), .en(decoder_1_out27), .clk(Clk), .Q(R27_q));  // open: clr
  Register R4 (.D(Write_Data), .en(decoder_1_out4), .clk(Clk), .Q(R4_q));  // open: clr
  Register R12 (.D(Write_Data), .en(decoder_1_out12), .clk(Clk), .Q(R12_q));  // open: clr
  Register R20 (.D(Write_Data), .en(decoder_1_out20), .clk(Clk), .Q(R20_q));  // open: clr
  Register R28 (.D(Write_Data), .en(decoder_1_out28), .clk(Clk), .Q(R28_q));  // open: clr
  Register R5 (.D(Write_Data), .en(decoder_1_out5), .clk(Clk), .Q(R5_q));  // open: clr
  Register R13 (.D(Write_Data), .en(decoder_1_out13), .clk(Clk), .Q(R13_q));  // open: clr
  Register R21 (.D(Write_Data), .en(decoder_1_out21), .clk(Clk), .Q(R21_q));  // open: clr
  Register R29 (.D(Write_Data), .en(decoder_1_out29), .clk(Clk), .Q(R29_q));  // open: clr
  Register R6 (.D(Write_Data), .en(decoder_1_out6), .clk(Clk), .Q(R6_q));  // open: clr
  Register R14 (.D(Write_Data), .en(decoder_1_out14), .clk(Clk), .Q(R14_q));  // open: clr
  Register R22 (.D(Write_Data), .en(decoder_1_out22), .clk(Clk), .Q(R22_q));  // open: clr
  Register R30 (.D(Write_Data), .en(decoder_1_out30), .clk(Clk), .Q(R30_q));  // open: clr
  Register R7 (.D(Write_Data), .en(decoder_1_out7), .clk(Clk), .Q(R7_q));  // open: clr
  Register R15 (.D(Write_Data), .en(decoder_1_out15), .clk(Clk), .Q(R15_q));  // open: clr
  Register R23 (.D(Write_Data), .en(decoder_1_out23), .clk(Clk), .Q(R23_q));  // open: clr
  Register R31 (.D(Write_Data), .en(decoder_1_out31), .clk(Clk), .Q(R31_q));  // open: clr
  Multiplexer #(.select(5), .width(8)) multiplexer_1 (
    .in0(R0_q), .in1(R1_q), .in2(R2_q), .in3(R3_q), .in4(R4_q), .in5(R5_q), .in6(R6_q), .in7(R7_q),
    .in8(R8_q), .in9(R9_q), .in10(R10_q), .in11(R11_q), .in12(R12_q), .in13(R13_q), .in14(R14_q),
    .in15(R15_q), .in16(R16_q), .in17(R17_q), .in18(R18_q), .in19(R19_q), .in20(R20_q), .in21(R21_q),
    .in22(R22_q), .in23(R23_q), .in24(R24_q), .in25(R25_q), .in26(R26_q), .in27(R27_q), .in28(R28_q),
    .in29(R29_q), .in30(R30_q), .in31(R31_q), .out(Read_Data_1), .sel(Read_address_1));
  Multiplexer #(.select(5), .width(8)) multiplexer_2 (
    .in0(R0_q), .in1(R1_q), .in2(R2_q), .in3(R3_q), .in4(R4_q), .in5(R5_q), .in6(R6_q), .in7(R7_q),
    .in8(R8_q), .in9(R9_q), .in10(R10_q), .in11(R11_q), .in12(R12_q), .in13(R13_q), .in14(R14_q),
    .in15(R15_q), .in16(R16_q), .in17(R17_q), .in18(R18_q), .in19(R19_q), .in20(R20_q), .in21(R21_q),
    .in22(R22_q), .in23(R23_q), .in24(R24_q), .in25(R25_q), .in26(R26_q), .in27(R27_q), .in28(R28_q),
    .in29(R29_q), .in30(R30_q), .in31(R31_q), .out(Read_Data_2), .sel(Read_address_2));

  // Notes on the sheet:
  //   Fig:32 register (8 bit)
endmodule

module ALU (
  input  [7:0] A,
  input  [7:0] B,
  input  [2:0] Shamt,
  input  [2:0] AluOpCode,
  output [7:0] Result,
  output Zero
);

  wire comparator_1_gt;
  wire [7:0] adder_1_out, adder_2_out, bit_extender_1_out, shifter_1_out, shifter_2_out, subtractor_1_out,
       xor_1_out;

  Adder adder_1 (.a(A), .b(B), .out(adder_1_out));  // open: cin, cout
  Subtractor subtractor_1 (.a(A), .b(B), .out(subtractor_1_out));  // open: bin, bout
  Adder adder_2 (.a(8'h1), .b(B), .out(adder_2_out));  // open: cin, cout
  Shifter shifter_1 (.in(A), .\dist (Shamt), .out(shifter_1_out));
  Shifter #(.shift("lr")) shifter_2 (.in(A), .\dist (Shamt), .out(shifter_2_out));
  assign xor_1_out = A ^ B;  // XOR_Gate xor_1, 8 bits wide
  Comparator comparator_1 (.a(A), .b(B), .gt(comparator_1_gt));  // open: eq, lt
  assign bit_extender_1_out = {{7{comparator_1_gt}}, comparator_1_gt};  // Bit_Extender bit_extender_1
  Multiplexer #(.select(3), .width(8)) multiplexer_1 (
    .in0(adder_1_out), .in1(subtractor_1_out), .in2(adder_2_out), .in3(shifter_1_out), .in4(shifter_2_out),
    .in5(xor_1_out), .in6(bit_extender_1_out), .out(Result), .sel(AluOpCode));  // open: in7
  nor nor_1 (Zero, Result[0], Result[1], Result[2], Result[3], Result[4], Result[5], Result[6], Result[7]);

  // Notes on the sheet:
  //   Fig: 8 bit ALU
endmodule

module Data_path (
);

  wire alu_1_zero, and_1_out, clock_1_out, control_unit_1_alusrc, control_unit_1_branch, control_unit_1_jump,
       control_unit_1_memread, control_unit_1_memtoreg, control_unit_1_memwrite, control_unit_1_regdest,
       control_unit_1_regwrite;
  wire [2:0] control_unit_1_aluop, Instruction_Memory_data_5;
  wire [3:0] Instruction_Memory_data_4;
  wire [4:0] Instruction_Memory_data, Instruction_Memory_data_2, Instruction_Memory_data_3, multiplexer_3_out;
  wire [7:0] adder_1_out, alu_1_result, bit_extender_1_out, Data_Memory_dout, multiplexer_1_out,
       multiplexer_2_out, multiplexer_4_out, multiplexer_5_out, PC_q, register_file_1_read_data_1,
       register_file_1_read_data_2;

  Clock clock_1 (.out(clock_1_out));
  Multiplexer #(.width(8)) multiplexer_1 (
    .in0(adder_1_out), .in1(bit_extender_1_out), .out(multiplexer_1_out), .sel(control_unit_1_jump));
  and and_1 (and_1_out, alu_1_zero, control_unit_1_branch);
  Register PC (.D(multiplexer_2_out), .clk(clock_1_out), .Q(PC_q));  // open: en, clr
  Multiplexer #(.width(8)) multiplexer_2 (
    .in0(multiplexer_1_out), .in1({Instruction_Memory_data, Instruction_Memory_data_5}),
    .out(multiplexer_2_out), .sel(and_1_out));
  Adder adder_1 (.a(8'h1), .b(PC_q), .out(adder_1_out));  // open: cin, cout
  ROM #(.dataWidth(22)) Instruction_Memory (
    .addr(PC_q),
    .data({Instruction_Memory_data_4, Instruction_Memory_data_3, Instruction_Memory_data_2, Instruction_Memory_data, Instruction_Memory_data_5}));
  Bit_Extender #(.in_width(18), .out_width(8), .\type ("zero")) bit_extender_1 (
    .in({Instruction_Memory_data_3, Instruction_Memory_data_2, Instruction_Memory_data, Instruction_Memory_data_5}),
    .out(bit_extender_1_out));
  Multiplexer #(.width(5)) multiplexer_3 (
    .in0(Instruction_Memory_data), .in1(Instruction_Memory_data_2), .out(multiplexer_3_out),
    .sel(control_unit_1_regdest));
  Multiplexer #(.width(8)) multiplexer_4 (
    .in0(alu_1_result), .in1(Data_Memory_dout), .out(multiplexer_4_out), .sel(control_unit_1_memtoreg));
  Control_Unit control_unit_1 (
    .Opcode(Instruction_Memory_data_4), .ALUOP(control_unit_1_aluop), .RegWrite(control_unit_1_regwrite),
    .RegDest(control_unit_1_regdest), .ALUSrc(control_unit_1_alusrc), .MemRead(control_unit_1_memread),
    .MemWrite(control_unit_1_memwrite), .MemToReg(control_unit_1_memtoreg), .Jump(control_unit_1_jump),
    .Branch(control_unit_1_branch));
  Register_File register_file_1 (
    .Write(control_unit_1_regwrite), .Write_address(multiplexer_3_out),
    .Read_address_1(Instruction_Memory_data_3), .Read_address_2(Instruction_Memory_data_2),
    .Clk(clock_1_out), .Write_Data(multiplexer_4_out), .Read_Data_2(register_file_1_read_data_2),
    .Read_Data_1(register_file_1_read_data_1));
  Multiplexer #(.width(8)) multiplexer_5 (
    .in0(register_file_1_read_data_2), .in1({Instruction_Memory_data, Instruction_Memory_data_5}),
    .out(multiplexer_5_out), .sel(control_unit_1_alusrc));
  ALU alu_1 (
    .A(register_file_1_read_data_1), .B(multiplexer_5_out), .Shamt(Instruction_Memory_data_5),
    .AluOpCode(control_unit_1_aluop), .Result(alu_1_result), .Zero(alu_1_zero));
  RAM #(.asyncread("true")) Data_Memory (
    .addr(alu_1_result), .we(control_unit_1_memwrite), .oe(control_unit_1_memread), .clk(clock_1_out),
    .din(register_file_1_read_data_2), .dout(Data_Memory_dout));

  // Notes on the sheet:
  //   Fig: Datapath 
endmodule

module Control_Unit (
  input  [3:0] Opcode,
  output [2:0] ALUOP,
  output RegWrite,
  output RegDest,
  output ALUSrc,
  output MemRead,
  output MemWrite,
  output MemToReg,
  output Jump,
  output Branch
);

  wire and_1_out, and_2_out, and_3_out, and_4_out, and_5_out, and_6_out, and_7_out, and_8_out, and_9_out,
       and_10_out, and_11_out, and_12_out, and_14_out, and_15_out, and_16_out, and_17_out, and_18_out,
       and_19_out, and_20_out, and_21_out, and_22_out, and_23_out, and_24_out, and_25_out, and_26_out,
       and_27_out, and_29_out, and_30_out, and_31_out, and_36_out, and_37_out, and_38_out, and_39_out,
       not_1_out, not_2_out, not_3_out, not_4_out, or_1_out, or_4_out, or_5_out, or_6_out, or_7_out,
       or_8_out, or_9_out;

  not not_1 (not_1_out, Opcode[3]);
  not not_2 (not_2_out, Opcode[2]);
  not not_3 (not_3_out, Opcode[1]);
  not not_4 (not_4_out, Opcode[0]);
  and and_1 (and_1_out, Opcode[2], Opcode[0]);
  and and_2 (and_2_out, Opcode[2], Opcode[1]);
  and and_3 (and_3_out, Opcode[3], Opcode[1]);
  and and_4 (and_4_out, Opcode[2], not_3_out);
  and and_5 (and_5_out, not_1_out, Opcode[1]);
  and and_6 (and_6_out, Opcode[3], not_3_out);
  and and_7 (and_7_out, Opcode[2], Opcode[1]);
  and and_8 (and_8_out, not_2_out, not_3_out);
  and and_9 (and_9_out, not_2_out, not_3_out);
  and and_10 (and_10_out, Opcode[3], Opcode[1]);
  and and_11 (and_11_out, Opcode[3], not_3_out);
  and and_12 (and_12_out, Opcode[3], Opcode[1]);
  and and_13 (MemToReg, Opcode[3], not_3_out);
  and and_14 (and_14_out, Opcode[2], Opcode[1]);
  and and_15 (and_15_out, Opcode[3], not_3_out);
  or or_1 (or_1_out, and_1_out, and_2_out);
  and and_16 (and_16_out, and_3_out, Opcode[0]);
  and and_17 (and_17_out, Opcode[1], Opcode[0]);
  and and_18 (and_18_out, and_4_out, not_4_out);
  and and_19 (and_19_out, and_5_out, not_4_out);
  and and_20 (and_20_out, and_6_out, not_4_out);
  and and_21 (and_21_out, Opcode[2], Opcode[1]);
  and and_22 (and_22_out, Opcode[3], Opcode[2]);
  and and_23 (and_23_out, not_1_out, Opcode[2]);
  and and_24 (and_24_out, not_1_out, not_3_out);
  and and_25 (and_25_out, not_2_out, Opcode[0]);
  and and_26 (and_26_out, and_7_out, not_4_out);
  and and_27 (and_27_out, not_1_out, not_2_out);
  and and_28 (RegDest, and_8_out, Opcode[0]);
  and and_29 (and_29_out, and_9_out, Opcode[0]);
  and and_30 (and_30_out, and_10_out, not_4_out);
  and and_31 (and_31_out, Opcode[2], Opcode[1]);
  and and_32 (MemRead, and_11_out, Opcode[0]);
  and and_33 (MemWrite, and_12_out, not_4_out);
  and and_34 (Jump, and_14_out, Opcode[0]);
  and and_35 (Branch, and_15_out, not_4_out);
  or or_2 (ALUOP[2], or_1_out, and_16_out);
  or or_3 (ALUOP[1], and_17_out, and_18_out);
  or or_4 (or_4_out, and_19_out, and_20_out);
  and and_36 (and_36_out, and_21_out, Opcode[0]);
  and and_37 (and_37_out, and_22_out, Opcode[0]);
  and and_38 (and_38_out, and_23_out, not_4_out);
  or or_5 (or_5_out, and_24_out, and_25_out);
  or or_6 (or_6_out, and_26_out, and_27_out);
  or or_7 (or_7_out, and_29_out, and_30_out);
  and and_39 (and_39_out, and_31_out, Opcode[0]);
  or or_8 (or_8_out, or_4_out, and_36_out);
  or or_9 (or_9_out, and_37_out, and_38_out);
  or or_10 (RegWrite, or_5_out, or_6_out);
  or or_11 (ALUSrc, or_7_out, and_39_out);
  or or_12 (ALUOP[0], or_8_out, or_9_out);

  // Notes on the sheet:
  //   Fig: Control Unit
endmodule
