// Logisim project aa.circ as structural Verilog: 5 circuits, main circuit main
module main (
  input  Clk,
  input  [7:0] Write_Data,
  input  Write,
  input  [4:0] Write_address,
  input  [4:0] Read_address_1,
  input  [4:0] Read_address_2,
  output [7:0] Read_Data_1,
  output [7:0] Read_Data_2
);

  wire decoder_1_out0, decoder_1_out1, decoder_1_out2, decoder_1_out3, decoder_1_out4, decoder_1_out5,
       decoder_1_out6, decoder_1_out7, decoder_1_out8, decoder_1_out9, decoder_1_out10, decoder_1_out11,
       decoder_1_out12, decoder_1_out13, decoder_1_out14, decoder_1_out15, decoder_1_out16, decoder_1_out17,
       decoder_1_out18, decoder_1_out19, decoder_1_out20, decoder_1_out21, decoder_1_out22, decoder_1_out23,
       decoder_1_out24, decoder_1_out25, decoder_1_out26, decoder_1_out27, decoder_1_out28, decoder_1_out29,
       decoder_1_out30, decoder_1_out31;
  wire [7:0] register_1_q, register_2_q, register_3_q, register_4_q, register_5_q, register_6_q,
       register_7_q, register_8_q, register_9_q, register_10_q, register_11_q, register_12_q, register_13_q,
       register_14_q, register_15_q, register_16_q, register_17_q, register_18_q, register_19_q,
       register_20_q, register_21_q, register_22_q, register_23_q, register_24_q, register_25_q,
       register_26_q, register_27_q, register_28_q, register_29_q, register_30_q, register_31_q,
       register_32_q;

  Decoder #(.select(5)) decoder_1 (
    .out0(decoder_1_out0), .out1(decoder_1_out1), .out2(decoder_1_out2), .out3(decoder_1_out3),
    .out4(decoder_1_out4), .out5(decoder_1_out5), .out6(decoder_1_out6), .out7(decoder_1_out7),
    .out8(decoder_1_out8), .out9(decoder_1_out9), .out10(decoder_1_out10), .out11(decoder_1_out11),
    .out12(decoder_1_out12), .out13(decoder_1_out13), .out14(decoder_1_out14), .out15(decoder_1_out15),
    .out16(decoder_1_out16), .out17(decoder_1_out17), .out18(decoder_1_out18), .out19(decoder_1_out19),
    .out20(decoder_1_out20), .out21(decoder_1_out21), .out22(decoder_1_out22), .out23(decoder_1_out23),
    .out24(decoder_1_out24), .out25(decoder_1_out25), .out26(decoder_1_out26), .out27(decoder_1_out27),
    .out28(decoder_1_out28), .out29(decoder_1_out29), .out30(decoder_1_out30), .out31(decoder_1_out31),
    .sel(Write_address), .en(Write));
  Register register_1 (.D(Write_Data), .en(decoder_1_out0), .clk(Clk), .Q(register_1_q));  // open: clr
  Register register_2 (.D(Write_Data), .en(decoder_1_out8), .clk(Clk), .Q(register_2_q));  // open: clr
  Register register_3 (.D(Write_Data), .en(decoder_1_out16), .clk(Clk), .Q(register_3_q));  // open: clr
  Register register_4 (.D(Write_Data), .en(decoder_1_out24), .clk(Clk), .Q(register_4_q));  // open: clr
  Register register_5 (.D(Write_Data), .en(decoder_1_out1), .clk(Clk), .Q(register_5_q));  // open: clr
  Register register_6 (.D(Write_Data), .en(decoder_1_out9), .clk(Clk), .Q(register_6_q));  // open: clr
  Register register_7 (.D(Write_Data), .en(decoder_1_out17), .clk(Clk), .Q(register_7_q));  // open: clr
  Register register_8 (.D(Write_Data), .en(decoder_1_out25), .clk(Clk), .Q(register_8_q));  // open: clr
  Register register_9 (.D(Write_Data), .en(decoder_1_out2), .clk(Clk), .Q(register_9_q));  // open: clr
  Register register_10 (.D(Write_Data), .en(decoder_1_out10), .clk(Clk), .Q(register_10_q));  // open: clr
  Register register_11 (.D(Write_Data), .en(decoder_1_out18), .clk(Clk), .Q(register_11_q));  // open: clr
  Register register_12 (.D(Write_Data), .en(decoder_1_out26), .clk(Clk), .Q(register_12_q));  // open: clr
  Register register_13 (.D(Write_Data), .en(decoder_1_out3), .clk(Clk), .Q(register_13_q));  // open: clr
  Register register_14 (.D(Write_Data), .en(decoder_1_out11), .clk(Clk), .Q(register_14_q));  // open: clr
  Register register_15 (.D(Write_Data), .en(decoder_1_out19), .clk(Clk), .Q(register_15_q));  // open: clr
  Register register_16 (.D(Write_Data), .en(decoder_1_out27), .clk(Clk), .Q(register_16_q));  // open: clr
  Register register_17 (.D(Write_Data), .en(decoder_1_out4), .clk(Clk), .Q(register_17_q));  // open: clr
  Register register_18 (.D(Write_Data), .en(decoder_1_out12), .clk(Clk), .Q(register_18_q));  // open: clr
  Register register_19 (.D(Write_Data), .en(decoder_1_out20), .clk(Clk), .Q(register_19_q));  // open: clr
  Register register_20 (.D(Write_Data), .en(decoder_1_out28), .clk(Clk), .Q(register_20_q));  // open: clr
  Register register_21 (.D(Write_Data), .en(decoder_1_out5), .clk(Clk), .Q(register_21_q));  // open: clr
  Register register_22 (.D(Write_Data), .en(decoder_1_out13), .clk(Clk), .Q(register_22_q));  // open: clr
  Register register_23 (.D(Write_Data), .en(decoder_1_out21), .clk(Clk), .Q(register_23_q));  // open: clr
  Register register_24 (.D(Write_Data), .en(decoder_1_out29), .clk(Clk), .Q(register_24_q));  // open: clr
  Register register_25 (.D(Write_Data), .en(decoder_1_out6), .clk(Clk), .Q(register_25_q));  // open: clr
  Register register_26 (.D(Write_Data), .en(decoder_1_out14), .clk(Clk), .Q(register_26_q));  // open: clr
  Register register_27 (.D(Write_Data), .en(decoder_1_out22), .clk(Clk), .Q(register_27_q));  // open: clr
  Register register_28 (.D(Write_Data), .en(decoder_1_out30), .clk(Clk), .Q(register_28_q));  // open: clr
  Register register_29 (.D(Write_Data), .en(decoder_1_out7), .clk(Clk), .Q(register_29_q));  // open: clr
  Register register_30 (.D(Write_Data), .en(decoder_1_out15), .clk(Clk), .Q(register_30_q));  // open: clr
  Register register_31 (.D(Write_Data), .en(decoder_1_out23), .clk(Clk), .Q(register_31_q));  // open: clr
  Register register_32 (.D(Write_Data), .en(decoder_1_out31), .clk(Clk), .Q(register_32_q));  // open: clr
  Multiplexer #(.select(5), .width(8)) multiplexer_1 (
    .in0(register_1_q), .in1(register_5_q), .in2(register_9_q), .in3(register_13_q), .in4(register_17_q),
    .in5(register_21_q), .in6(register_25_q), .in7(register_29_q), .in8(register_2_q), .in9(register_6_q),
    .in10(register_10_q), .in11(register_14_q), .in12(register_18_q), .in13(register_22_q),
    .in14(register_26_q), .in15(register_30_q), .in16(register_3_q), .in17(register_7_q),
    .in18(register_11_q), .in19(register_15_q), .in20(register_19_q), .in21(register_23_q),
    .in22(register_27_q), .in23(register_31_q), .in24(register_4_q), .in25(register_8_q),
    .in26(register_12_q), .in27(register_16_q), .in28(register_20_q), .in29(register_24_q),
    .in30(register_28_q), .in31(register_32_q), .out(Read_Data_1), .sel(Read_address_1));
  Multiplexer #(.select(5), .width(8)) multiplexer_2 (
    .in0(register_1_q), .in1(register_5_q), .in2(register_9_q), .in3(register_13_q), .in4(register_17_q),
    .in5(register_21_q), .in6(register_25_q), .in7(register_29_q), .in8(register_2_q), .in9(register_6_q),
    .in10(register_10_q), .in11(register_14_q), .in12(register_18_q), .in13(register_22_q),
    .in14(register_26_q), .in15(register_30_q), .in16(register_3_q), .in17(register_7_q),
    .in18(register_11_q), .in19(register_15_q), .in20(register_19_q), .in21(register_23_q),
    .in22(register_27_q), .in23(register_31_q), .in24(register_4_q), .in25(register_8_q),
    .in26(register_12_q), .in27(register_16_q), .in28(register_20_q), .in29(register_24_q),
    .in30(register_28_q), .in31(register_32_q), .out(Read_Data_2), .sel(Read_address_2));
endmodule

module ALU (
  input  [7:0] A,
  input  [7:0] B,
  input  [2:0] Shamt,
  input  [2:0] AluOpCode,
  output [7:0] Result,
  output Zero
);

  wire comparator_1_gt;
  wire [7:0] adder_1_out, adder_2_out, bit_extender_1_out, shifter_1_out, shifter_2_out, subtractor_1_out,
       xor_1_out;

  Comparator comparator_1 (.a(A), .b(B), .gt(comparator_1_gt));  // open: eq, lt
  Adder adder_1 (.a(A), .b(B), .out(adder_1_out));  // open: cin, cout
  Subtractor subtractor_1 (.a(A), .b(B), .out(subtractor_1_out));  // open: bin, bout
  Adder adder_2 (.a(8'h1), .b(B), .out(adder_2_out));  // open: cin, cout
  Shifter shifter_1 (.in(A), .\dist (Shamt), .out(shifter_1_out));
  Shifter #(.shift("lr")) shifter_2 (.in(A), .\dist (Shamt), .out(shifter_2_out));
  assign xor_1_out = A ^ B;  // XOR_Gate xor_1, 8 bits wide
  assign bit_extender_1_out = {{7{comparator_1_gt}}, comparator_1_gt};  // Bit_Extender bit_extender_1
  Multiplexer #(.select(3), .width(8)) multiplexer_1 (
    .in0(adder_1_out), .in1(subtractor_1_out), .in2(adder_2_out), .in3(shifter_1_out), .in4(shifter_2_out),
    .in5(xor_1_out), .in6(bit_extender_1_out), .out(Result), .sel(AluOpCode));  // open: in7
  nor nor_1 (Zero, Result[0], Result[1], Result[2], Result[3], Result[4], Result[5], Result[6], Result[7]);
endmodule

module Data_path (
);

  wire alu_1_zero, and_1_out, clock_1_out, mm_1_alusrc, mm_1_branch, mm_1_jump, mm_1_memread, mm_1_memtoreg,
       mm_1_memwrite, mm_1_regdest, mm_1_regwrite;
  wire [2:0] mm_1_aluop, rom_1_data_5;
  wire [3:0] rom_1_data_4;
  wire [4:0] multiplexer_3_out, rom_1_data, rom_1_data_2, rom_1_data_3;
  wire [7:0] adder_1_out, alu_1_result, bit_extender_1_out, main_1_read_data_1, main_1_read_data_2,
       multiplexer_1_out, multiplexer_2_out, multiplexer_4_out, multiplexer_5_out, ram_1_dout, register_1_q;

  Clock clock_1 (.out(clock_1_out));
  Multiplexer #(.width(8)) multiplexer_1 (
    .in0(adder_1_out), .in1(bit_extender_1_out), .out(multiplexer_1_out), .sel(mm_1_jump));
  and and_1 (and_1_out, alu_1_zero, mm_1_branch);
  Register register_1 (.D(multiplexer_2_out), .clk(clock_1_out), .Q(register_1_q));  // open: en, clr
  Multiplexer #(.width(8)) multiplexer_2 (
    .in0(multiplexer_1_out), .in1({rom_1_data, rom_1_data_5}), .out(multiplexer_2_out), .sel(and_1_out));
  Adder adder_1 (.a(8'h1), .b(register_1_q), .out(adder_1_out));  // open: cin, cout
  ROM #(.dataWidth(22)) rom_1 (
    .addr(register_1_q), .data({rom_1_data_4, rom_1_data_3, rom_1_data_2, rom_1_data, rom_1_data_5}));
  Bit_Extender #(.in_width(18), .out_width(8), .\type ("zero")) bit_extender_1 (
    .in({rom_1_data_3, rom_1_data_2, rom_1_data, rom_1_data_5}), .out(bit_extender_1_out));
  Multiplexer #(.width(5)) multiplexer_3 (
    .in0(rom_1_data), .in1(rom_1_data_2), .out(multiplexer_3_out), .sel(mm_1_regdest));
  Multiplexer #(.width(8)) multiplexer_4 (
    .in0(alu_1_result), .in1(ram_1_dout), .out(multiplexer_4_out), .sel(mm_1_memtoreg));
  mm mm_1 (
    .Opcode(rom_1_data_4), .ALUOP(mm_1_aluop), .RegWrite(mm_1_regwrite), .RegDest(mm_1_regdest),
    .ALUSrc(mm_1_alusrc), .MemRead(mm_1_memread), .MemWrite(mm_1_memwrite), .MemToReg(mm_1_memtoreg),
    .Jump(mm_1_jump), .Branch(mm_1_branch));
  main main_1 (
    .Write(mm_1_regwrite), .Write_address(multiplexer_3_out), .Read_address_1(rom_1_data_3),
    .Read_address_2(rom_1_data_2), .Clk(clock_1_out), .Write_Data(multiplexer_4_out),
    .Read_Data_2(main_1_read_data_2), .Read_Data_1(main_1_read_data_1));
  Multiplexer #(.width(8)) multiplexer_5 (
    .in0(main_1_read_data_2), .in1({rom_1_data, rom_1_data_5}), .out(multiplexer_5_out), .sel(mm_1_alusrc));
  ALU alu_1 (
    .A(main_1_read_data_1), .B(multiplexer_5_out), .Shamt(rom_1_data_5), .AluOpCode(mm_1_aluop),
    .Result(alu_1_result), .Zero(alu_1_zero));
  RAM #(.asyncread("true")) ram_1 (
    .addr(alu_1_result), .we(mm_1_memwrite), .oe(mm_1_memread), .clk(clock_1_out), .din(main_1_read_data_2),
    .dout(ram_1_dout));

  // Notes on the sheet:
  //   contents of rom_1 (hex, n*v repeats v):
  //   40100 40204 40300 4040a 40505 40601 20240e 6218 28a201 4a501 44204 42101 28c30f 1c0006
endmodule

module Control_Unit (
  input  [3:0] Opcode,
  output [2:0] ALUOP,
  output RegWrite,
  output RegDest,
  output ALUSrc,
  output MemRead,
  output MemWrite,
  output MemToReg,
  output Jump,
  output Branch
);

  wire and_1_out, and_2_out, and_3_out, and_4_out, and_5_out, and_6_out, and_7_out, and_8_out, and_9_out,
       and_10_out, and_11_out, and_12_out, and_13_out, and_14_out, and_15_out, and_16_out, and_17_out,
       and_18_out, and_19_out, and_20_out, and_21_out, and_22_out, and_23_out, and_24_out, and_25_out,
       and_26_out, and_27_out, and_28_out, and_29_out, and_30_out, and_31_out, and_32_out, and_33_out,
       and_34_out, and_35_out, and_36_out, and_37_out, and_38_out, and_41_out, and_42_out, and_43_out,
       and_44_out, and_45_out, not_1_out, not_2_out, not_3_out, not_4_out, or_2_out, or_3_out, or_4_out,
       or_5_out, or_7_out, or_11_out, or_12_out;

  not not_1 (not_1_out, Opcode[3]);
  not not_2 (not_2_out, Opcode[2]);
  not not_3 (not_3_out, Opcode[1]);
  not not_4 (not_4_out, Opcode[0]);
  and and_1 (and_1_out, not_1_out, Opcode[2]);
  and and_2 (and_2_out, not_1_out, not_2_out);
  and and_3 (and_3_out, Opcode[1], Opcode[0]);
  and and_4 (and_4_out, Opcode[2], not_3_out);
  and and_5 (and_5_out, not_1_out, Opcode[1]);
  and and_6 (and_6_out, Opcode[3], not_3_out);
  and and_7 (and_7_out, Opcode[2], Opcode[1]);
  and and_8 (and_8_out, not_2_out, not_3_out);
  and and_9 (and_9_out, not_2_out, not_3_out);
  and and_10 (and_10_out, Opcode[3], Opcode[1]);
  and and_11 (and_11_out, Opcode[3], not_2_out);
  and and_12 (and_12_out, Opcode[3], Opcode[2]);
  and and_13 (and_13_out, Opcode[3], not_2_out);
  and and_14 (and_14_out, Opcode[3], Opcode[2]);
  and and_15 (and_15_out, Opcode[2], Opcode[1]);
  and and_16 (and_16_out, Opcode[3], not_3_out);
  and and_17 (and_17_out, and_1_out, Opcode[0]);
  and and_18 (and_18_out, Opcode[2], Opcode[1]);
  and and_19 (and_19_out, and_2_out, and_3_out);
  and and_20 (and_20_out, and_4_out, not_4_out);
  and and_21 (and_21_out, Opcode[3], Opcode[2]);
  and and_22 (and_22_out, and_5_out, not_4_out);
  and and_23 (and_23_out, and_6_out, not_4_out);
  and and_24 (and_24_out, Opcode[2], Opcode[1]);
  and and_25 (and_25_out, Opcode[3], Opcode[2]);
  and and_26 (and_26_out, not_1_out, Opcode[2]);
  and and_27 (and_27_out, not_1_out, not_3_out);
  and and_28 (and_28_out, not_2_out, Opcode[0]);
  and and_29 (and_29_out, and_7_out, not_4_out);
  and and_30 (and_30_out, not_1_out, not_2_out);
  and and_31 (and_31_out, and_8_out, Opcode[0]);
  and and_32 (and_32_out, and_9_out, Opcode[0]);
  and and_33 (and_33_out, and_10_out, not_4_out);
  and and_34 (and_34_out, Opcode[2], Opcode[1]);
  and and_35 (and_35_out, and_11_out, Opcode[0]);
  and and_36 (and_36_out, and_12_out, Opcode[1]);
  and and_37 (and_37_out, and_13_out, Opcode[1]);
  and and_38 (and_38_out, and_14_out, Opcode[0]);
  and and_39 (Jump, and_15_out, Opcode[0]);
  and and_40 (Branch, and_16_out, not_4_out);
  or or_1 (ALUOP[2], and_17_out, and_18_out);
  or or_2 (or_2_out, and_19_out, and_20_out);
  and and_41 (and_41_out, and_21_out, not_3_out);
  or or_3 (or_3_out, and_22_out, and_23_out);
  and and_42 (and_42_out, and_24_out, Opcode[0]);
  and and_43 (and_43_out, and_25_out, Opcode[0]);
  and and_44 (and_44_out, and_26_out, not_4_out);
  or or_4 (or_4_out, and_27_out, and_28_out);
  or or_5 (or_5_out, and_29_out, and_30_out);
  or or_6 (RegDest, and_31_out, Opcode[3]);
  or or_7 (or_7_out, and_32_out, and_33_out);
  and and_45 (and_45_out, and_34_out, Opcode[0]);
  or or_8 (MemRead, and_35_out, and_36_out);
  or or_9 (MemWrite, and_37_out, and_38_out);
  or or_10 (ALUOP[1], or_2_out, and_41_out);
  or or_11 (or_11_out, or_3_out, and_42_out);
  or or_12 (or_12_out, and_43_out, and_44_out);
  or or_13 (RegWrite, or_4_out, or_5_out);
  or or_14 (ALUSrc, or_7_out, and_45_out);
  or or_15 (ALUOP[0], or_11_out, or_12_out);

  assign MemToReg = Opcode[3];
endmodule

module mm (
  input  [3:0] Opcode,
  output [2:0] ALUOP,
  output RegWrite,
  output RegDest,
  output ALUSrc,
  output MemRead,
  output MemWrite,
  output MemToReg,
  output Jump,
  output Branch
);

  wire and_1_out, and_2_out, and_3_out, and_4_out, and_5_out, and_6_out, and_7_out, and_8_out, and_9_out,
       and_10_out, and_11_out, and_12_out, and_13_out, and_14_out, and_15_out, and_16_out, and_17_out,
       and_18_out, and_19_out, and_20_out, and_21_out, and_22_out, and_23_out, and_24_out, and_25_out,
       and_26_out, and_27_out, and_28_out, and_29_out, and_30_out, and_31_out, and_32_out, and_33_out,
       and_34_out, and_35_out, and_36_out, and_37_out, and_38_out, and_41_out, and_42_out, and_43_out,
       and_44_out, and_45_out, not_1_out, not_2_out, not_3_out, not_4_out, or_2_out, or_3_out, or_4_out,
       or_5_out, or_7_out, or_11_out, or_12_out;

  not not_1 (not_1_out, Opcode[3]);
  not not_2 (not_2_out, Opcode[2]);
  not not_3 (not_3_out, Opcode[1]);
  not not_4 (not_4_out, Opcode[0]);
  and and_1 (and_1_out, not_1_out, Opcode[2]);
  and and_2 (and_2_out, not_1_out, not_2_out);
  and and_3 (and_3_out, Opcode[1], Opcode[0]);
  and and_4 (and_4_out, Opcode[2], not_3_out);
  and and_5 (and_5_out, not_1_out, Opcode[1]);
  and and_6 (and_6_out, Opcode[3], not_3_out);
  and and_7 (and_7_out, Opcode[2], Opcode[1]);
  and and_8 (and_8_out, not_2_out, not_3_out);
  and and_9 (and_9_out, not_2_out, not_3_out);
  and and_10 (and_10_out, Opcode[3], Opcode[1]);
  and and_11 (and_11_out, Opcode[3], not_2_out);
  and and_12 (and_12_out, Opcode[3], Opcode[2]);
  and and_13 (and_13_out, Opcode[3], not_2_out);
  and and_14 (and_14_out, Opcode[3], Opcode[2]);
  and and_15 (and_15_out, Opcode[2], Opcode[1]);
  and and_16 (and_16_out, Opcode[3], not_3_out);
  and and_17 (and_17_out, and_1_out, Opcode[0]);
  and and_18 (and_18_out, Opcode[2], Opcode[1]);
  and and_19 (and_19_out, and_2_out, and_3_out);
  and and_20 (and_20_out, and_4_out, not_4_out);
  and and_21 (and_21_out, Opcode[3], Opcode[2]);
  and and_22 (and_22_out, and_5_out, not_4_out);
  and and_23 (and_23_out, and_6_out, not_4_out);
  and and_24 (and_24_out, Opcode[2], Opcode[1]);
  and and_25 (and_25_out, Opcode[3], Opcode[2]);
  and and_26 (and_26_out, not_1_out, Opcode[2]);
  and and_27 (and_27_out, not_1_out, not_3_out);
  and and_28 (and_28_out, not_2_out, Opcode[0]);
  and and_29 (and_29_out, and_7_out, not_4_out);
  and and_30 (and_30_out, not_1_out, not_2_out);
  and and_31 (and_31_out, and_8_out, Opcode[0]);
  and and_32 (and_32_out, and_9_out, Opcode[0]);
  and and_33 (and_33_out, and_10_out, not_4_out);
  and and_34 (and_34_out, Opcode[2], Opcode[1]);
  and and_35 (and_35_out, and_11_out, Opcode[0]);
  and and_36 (and_36_out, and_12_out, Opcode[1]);
  and and_37 (and_37_out, and_13_out, Opcode[1]);
  and and_38 (and_38_out, and_14_out, Opcode[0]);
  and and_39 (Jump, and_15_out, Opcode[0]);
  and and_40 (Branch, and_16_out, not_4_out);
  or or_1 (ALUOP[2], and_17_out, and_18_out);
  or or_2 (or_2_out, and_19_out, and_20_out);
  and and_41 (and_41_out, and_21_out, not_3_out);
  or or_3 (or_3_out, and_22_out, and_23_out);
  and and_42 (and_42_out, and_24_out, Opcode[0]);
  and and_43 (and_43_out, and_25_out, Opcode[0]);
  and and_44 (and_44_out, and_26_out, not_4_out);
  or or_4 (or_4_out, and_27_out, and_28_out);
  or or_5 (or_5_out, and_29_out, and_30_out);
  or or_6 (RegDest, and_31_out, Opcode[3]);
  or or_7 (or_7_out, and_32_out, and_33_out);
  and and_45 (and_45_out, and_34_out, Opcode[0]);
  or or_8 (MemRead, and_35_out, and_36_out);
  or or_9 (MemWrite, and_37_out, and_38_out);
  or or_10 (ALUOP[1], or_2_out, and_41_out);
  or or_11 (or_11_out, or_3_out, and_42_out);
  or or_12 (or_12_out, and_43_out, and_44_out);
  or or_13 (RegWrite, or_4_out, or_5_out);
  or or_14 (ALUSrc, or_7_out, and_45_out);
  or or_15 (ALUOP[0], or_11_out, or_12_out);

  assign MemToReg = Opcode[3];
endmodule
